// Digital circuit main.dig as structural Verilog
module main (
  input  [7:0] Instruction_Binary,
  input  clk,
  input  Write_instruction,
  input  [7:0] Starting_address,
  input  in_6,
  output [7:0] out_2
);

  wire u_do_once_data_out;
  wire [7:0] u_counter_8bit_count;

  do_once #(.applicationType("IVERILOG"), .CodeFile("/home/kaldwin/Development/Projects/the_electronics_project_misc/src/do_once.v")) u_do_once (
    .clk(clk), .data_in(clk), .reset(in_6), .data_out(u_do_once_data_out));  // open: ocurred
  counter_8bit #(.applicationType("IVERILOG"), .CodeFile("/home/kaldwin/Development/Projects/the_electronics_project_misc/src/counter_8bit.v")) u_counter_8bit (
    .clk(clk), .num(Starting_address), .load(Write_instruction), .reset(u_do_once_data_out),
    .count(u_counter_8bit_count));
  memory_256x8 #(.applicationType("IVERILOG"), .CodeFile("/home/kaldwin/Development/Projects/the_electronics_project_misc/src/memory_256x8.v")) u_memory_256x8 (
    .clk(clk), .write(Write_instruction), .address(u_counter_8bit_count), .data_in(Instruction_Binary),
    .data_out(out_2));

  // Notes on the sheet:
  //   clk: Hz: 5
endmodule
